// Digital circuit addr_gen.dig as structural Verilog
module addr_gen (
  input  [3:0] zero,
  input  [3:0] data__bus,
  input  clk,
  input  reset,
  input  brz,
  input  jump,
  input  use__pc,
  input  load__mar,
  output [3:0] addr__bus
);

  wire and_1_out, not_1_out, or_1_out, zero_t;
  wire [3:0] mar, pc;

  and and_1 (and_1_out, brz, zero_t);
  or or_1 (or_1_out, and_1_out, jump);
  nor nor_1 (zero_t, zero[3], zero[2], zero[1], zero[0], 1'b0);
  program_ctr program_ctr_1 (
    .load__pc(or_1_out), .enable(use__pc), .reset(reset), .clk(clk), .data__bus(data__bus), .q(pc));
  four_bit_reg u_MAR (.d(data__bus), .enable(load__mar), .reset(reset), .clk(clk), .q(mar));
  not not_1 (not_1_out, use__pc);
  four_bit_mux four_bit_mux_1 (.a(pc), .b(mar), .sel(not_1_out), .y(addr__bus));
endmodule
