// Digital circuit two_bit_reg.dig as structural Verilog
module two_bit_reg (
  input  [1:0] d,
  input  enable,
  input  reset,
  input  clk,
  output [1:0] y
);

  wire [1:0] two_bit_bus_mux_1_y;

  two_bit_bus_mux two_bit_bus_mux_1 (.a(y), .b(d), .sel(enable), .y(two_bit_bus_mux_1_y));
  D_FF_AS d_ff_as_1 (.Set(1'b0), .D(two_bit_bus_mux_1_y[1]), .C(clk), .Clr(reset), .Q(y[1]));  // open: nQ
  D_FF_AS d_ff_as_2 (.Set(1'b0), .D(two_bit_bus_mux_1_y[0]), .C(clk), .Clr(reset), .Q(y[0]));  // open: nQ
endmodule
