// Digital circuit two_bit_bus_mux.dig as structural Verilog
module two_bit_bus_mux (
  input  [1:0] a,
  input  [1:0] b,
  input  sel,
  output [1:0] y
);

  two_bit_mux two_bit_mux_1 (.a(a[1]), .b(b[1]), .s(sel), .y(y[1]));
  two_bit_mux two_bit_mux_2 (.a(a[0]), .b(b[0]), .s(sel), .y(y[0]));
endmodule
