// Digital circuit microprocessor.dig as structural Verilog
module microprocessor (
  input  clk,
  input  [3:0] data__in,
  input  reset,
  output [6:0] addr__bus,
  output [6:0] accum,
  output [6:0] data__bus,
  output [6:0] instr__reg
);

  wire not_1_out;
  wire [3:0] addr_gen_1_addr__bus, brainless_1_accum, brainless_1_data__bus, brainless_1_zero,
       controller_1_instr__reg;
  wire [11:0] controller_1_control;

  not not_1 (not_1_out, reset);
  addr_gen addr_gen_1 (
    .zero(brainless_1_zero), .data__bus(brainless_1_data__bus), .clk(clk), .reset(not_1_out),
    .brz(controller_1_control[11]), .jump(controller_1_control[10]), .use__pc(controller_1_control[9]),
    .load__mar(controller_1_control[8]), .addr__bus(addr_gen_1_addr__bus));
  controller controller_1 (
    .clk(clk), .reset(not_1_out), .data__bus(brainless_1_data__bus), .load__ir(controller_1_control[0]),
    .control(controller_1_control), .instr__reg(controller_1_instr__reg));
  brainless brainless_1 (
    .addr__bus(addr_gen_1_addr__bus), .data__in(data__in), .arith(controller_1_control[7]),
    .invert(controller_1_control[6]), .pass(controller_1_control[5]), .load__acc(controller_1_control[4]),
    .acc__to__db(controller_1_control[3]), .read(controller_1_control[2]), .write(controller_1_control[1]),
    .clk(clk), .reset(not_1_out), .zero(brainless_1_zero), .accum(brainless_1_accum),
    .data__bus(brainless_1_data__bus));  // open: alu__out
  segments segments_1 (.hex__in(addr_gen_1_addr__bus), .segs__out(addr__bus));
  segments segments_2 (.hex__in(brainless_1_accum), .segs__out(accum));
  segments segments_3 (.hex__in(brainless_1_data__bus), .segs__out(data__bus));
  segments segments_4 (.hex__in(controller_1_instr__reg), .segs__out(instr__reg));

  // Notes on the sheet:
  //   clk: pin B8
  //   data__in: pin C10, C11, D12, C12
  //   reset: pin A7
  //   addr__bus: pin C18, D18, E18, B16, A17, A18, B17
  //   accum: pin J20, K20, L18, N18, M20, N19, N20
  //   data__bus: pin C14, E15, C15, C16, E16, D17, C17
  //   instr__reg: pin B20, A20, B19, A21, B21, C22, B22
endmodule
